// Logisim project 4BitParity.circ as structural Verilog: 5 circuits, main circuit main
module main (
  input  Halt_Enable
);

  wire and_2_out, CLK, Correct, Done_Testing, Halt, Input, not_1_out, not_2_out, not_3_out, Solution,
       YourAnswer;
  wire [6:0] counter_1_q, TestNumber;

  not not_1 (not_1_out, Correct);
  Clock clock_1 (.out(CLK));
  and and_1 (Halt, Halt_Enable, not_1_out);
  Inputs inputs_1 (.Halt(Halt), .CLK(CLK), .Input(Input), .TestNumber(TestNumber), .Done_Testing(Done_Testing));
  _4BitEvenParity u_4bitevenparity_1 (.Input(Input), .CLK(CLK), .Is_Even(YourAnswer));
  // Probe on Input
  // Probe on YourAnswer
  // Probe on Solution
  // Probe on Correct
  not not_2 (not_2_out, Halt);
  and and_2 (and_2_out, Correct, not_2_out, not_3_out);
  not not_3 (not_3_out, Done_Testing);
  Checker checker_1 (.Your_Answer(YourAnswer), .TestNumber(TestNumber), .Correct(Correct), .Solution(Solution));
  Counter #(.width(7), .max('h41), .ongoal("stay")) counter_1 (
    .count(and_2_out), .Q(counter_1_q), .clk(CLK));  // open: load, D, carry, clr
  // Probe on counter_1_q

  // Notes on the sheet:
  //   Max 65
  //   Sayed Sadat (914290757)
  //   Muhammed Halbutogullari (913938544)
endmodule

module _4BitEvenParity (
  input  Input,
  input  CLK,
  output Is_Even
);

  wire [2:0] Current, sub_1_s0;

  // Probe on Current
  sub sub_1 (
    .i0(Current[0]), .i1(Current[1]), .i2(Current[2]), .\input (Input), .s0(sub_1_s0[0]), .s1(sub_1_s0[1]),
    .s2(sub_1_s0[2]));
  // Probe on Current
  Register #(.width(3)) STATE (.D(sub_1_s0), .Q(Current), .clk(CLK));  // open: en, clr
  and and_1 (Is_Even, Current[0], Current[1], Current[2]);
endmodule

module Inputs (
  input  Halt,
  input  CLK,
  output Input,
  output [6:0] TestNumber,
  output Done_Testing
);

  wire not_1_out;

  not not_1 (not_1_out, Halt);
  Counter #(.width(7), .max('h41), .ongoal("stay")) counter_1 (
    .count(not_1_out), .Q(TestNumber), .carry(Done_Testing), .clk(CLK));  // open: load, D, clr
  ROM #(.addrWidth(7), .dataWidth(1)) rom_1 (.addr(TestNumber), .data(Input));  // open: sel

  // Notes on the sheet:
  //   contents of rom_1 (hex, n*v repeats v):
  //   7*0 1 0 0 1 0 0 0 1 1 0 1 0 0 0 1 0 1 0 1 1 0 0 4*1 0 0 0 1 0 0 1 1 0 1 0 1 0 4*1 0 0 1 1 0 4*1 0
  //   4*1
endmodule

module Checker (
  input  Your_Answer,
  input  [6:0] TestNumber,
  output Correct,
  output Solution
);

  ROM #(.addrWidth(7), .dataWidth(1)) rom_1 (.addr(TestNumber), .data(Solution));  // open: sel
  Comparator #(.width(1)) comparator_1 (.a(Solution), .b(Your_Answer), .eq(Correct));  // open: gt, lt

  // Notes on the sheet:
  //   contents of rom_1 (hex, n*v repeats v):
  //   4*0 1 11*0 1 7*0 1 0 0 0 1 11*0 1 0 0 0 1 7*0 1 11*0 1
endmodule

module sub (
  input  i0,
  input  i1,
  input  i2,
  input  \input ,
  output s0,
  output s1,
  output s2
);

  wire and_1_out, and_2_out, and_3_out, and_4_out, and_5_out, and_6_out, and_7_out, and_8_out, and_9_out,
       and_10_out, and_11_out, and_12_out, and_13_out, not_1_out, not_2_out, not_3_out, not_4_out, not_5_out,
       not_6_out, not_7_out, not_8_out, not_9_out, not_10_out, not_11_out, not_12_out, not_13_out,
       not_14_out, not_15_out, not_16_out, not_17_out, not_18_out, not_19_out, not_20_out;

  not not_1 (not_1_out, i0);
  and and_1 (and_1_out, not_1_out, i2, \input );
  not not_2 (not_2_out, i0);
  and and_2 (and_2_out, not_2_out, i1, not_3_out);
  not not_3 (not_3_out, \input );
  and and_3 (and_3_out, i0, not_4_out, not_5_out);
  not not_4 (not_4_out, i1);
  not not_5 (not_5_out, i2);
  not not_6 (not_6_out, i1);
  and and_4 (and_4_out, i0, not_6_out, not_7_out);
  not not_7 (not_7_out, \input );
  and and_5 (and_5_out, i0, not_8_out, \input );
  not not_8 (not_8_out, i2);
  not not_9 (not_9_out, i0);
  not not_10 (not_10_out, i2);
  and and_6 (and_6_out, not_9_out, not_10_out, \input );
  not not_11 (not_11_out, i1);
  and and_7 (and_7_out, not_11_out, i2, not_12_out);
  not not_12 (not_12_out, \input );
  and and_8 (and_8_out, i1, \input );
  not not_13 (not_13_out, i1);
  and and_9 (and_9_out, i0, not_13_out, not_14_out);
  not not_14 (not_14_out, \input );
  not not_15 (not_15_out, i0);
  not not_16 (not_16_out, i1);
  and and_10 (and_10_out, not_15_out, not_16_out, not_17_out);
  not not_17 (not_17_out, \input );
  and and_11 (and_11_out, i2, not_18_out);
  not not_18 (not_18_out, \input );
  and and_12 (and_12_out, i1, not_19_out, \input );
  not not_19 (not_19_out, i2);
  not not_20 (not_20_out, i2);
  and and_13 (and_13_out, i0, not_20_out, \input );
  or or_1 (s0, and_1_out, and_2_out, and_3_out, and_4_out, and_5_out);
  or or_2 (s1, and_6_out, and_7_out, and_8_out, and_9_out);
  or or_3 (s2, and_10_out, and_11_out, and_12_out, and_13_out);
endmodule
