// Logisim project CPU.circ as structural Verilog: 4 circuits, main circuit CPU
module CPU (
);

  wire CLK, Halt, not_1_out, Regwrite;
  wire [3:0] A, Answer, C, Chosen_B, Immediate_B, OpCode, Reg_File_a_data, Register_B;
  wire [4:0] counter_1_q;
  wire [15:0] rom_1_data;

  Clock clock_1 (.out(CLK));
  Counter #(.width(5), .max('h1f)) counter_1 (
    .D({5{1'b0}}), .count(not_1_out), .Q(counter_1_q), .clk(CLK));  // open: load, carry, clr
  not not_1 (not_1_out, Halt);
  // Probe on counter_1_q
  ROM #(.addrWidth(5), .dataWidth(16)) rom_1 (.addr(counter_1_q), .data(rom_1_data));  // open: sel
  Decoder Decoder (
    .Input(rom_1_data), .Register_B(Register_B), .Immediate_B(Immediate_B), .A(A), .C(C), .Opcode(OpCode),
    .Halt(Halt), .RegWrite(Regwrite), .Chosen_B(Chosen_B));
  Reg_File Reg_File (
    .A(A), .B(Immediate_B), .C(C), .Data_In(Answer), .Reg_Write(Regwrite), .CLK(CLK),
    .A_DATA(Reg_File_a_data), .B_DATA(Register_B));
  ALU ALU (.OpCode(OpCode), .A(Reg_File_a_data), .B(Chosen_B), .Answer(Answer));

  // Notes on the sheet:
  //   Counter acts as a PC, and  iterates through the instructions until a halt
  //   Instructions
  //   contents of rom_1 (hex, n*v repeats v):
  //   2003 2106 1005 3210 4301 5433 6520 763c 8720 986f b938 ca77 db13 ec62 fd85 e05
  //   Sayed Yoseph Sadat 914290757
  //   Muhammed Halbutogullari (913938544) 
  //   ALU Recieves input based on operation, and outputs the result of the operation on these inputs
endmodule

module Reg_File (
  input  [3:0] A,
  input  [3:0] B,
  input  [3:0] C,
  input  [3:0] Data_In,
  input  Reg_Write,
  input  CLK,
  output [3:0] A_DATA,
  output [3:0] B_DATA
);

  wire Write_Reg0, Write_Reg1, Write_Reg2, Write_Reg3, Write_Reg4, Write_Reg5, Write_Reg6, Write_Reg7,
       Write_Reg8, Write_Reg9, Write_Reg10, Write_Reg11, Write_Reg12, Write_Reg13, Write_Reg14, Write_Reg15;
  wire [3:0] Reg0, Reg1, Reg2, Reg3, Reg4, Reg5, Reg6, Reg7, Reg8, Reg9, Reg10, Reg11, Reg12, Reg13, Reg14,
       Reg15;

  Demultiplexer #(.select(4), .enable("false")) demultiplexer_1 (
    .out0(Write_Reg0), .out1(Write_Reg1), .out2(Write_Reg2), .out3(Write_Reg3), .out4(Write_Reg4),
    .out5(Write_Reg5), .out6(Write_Reg6), .out7(Write_Reg7), .out8(Write_Reg8), .out9(Write_Reg9),
    .out10(Write_Reg10), .out11(Write_Reg11), .out12(Write_Reg12), .out13(Write_Reg13), .out14(Write_Reg14),
    .out15(Write_Reg15), .in(Reg_Write), .sel(C));
  // Probe on Reg0
  Register #(.width(4)) u_Reg0 (.D(Data_In), .en(Write_Reg0), .Q(Reg0), .clk(CLK));  // open: clr
  // Probe on Reg4
  Register #(.width(4)) u_Reg4 (.D(Data_In), .en(Write_Reg4), .Q(Reg4), .clk(CLK));  // open: clr
  // Probe on Reg8
  Register #(.width(4)) u_Reg8 (.D(Data_In), .en(Write_Reg8), .Q(Reg8), .clk(CLK));  // open: clr
  // Probe on Reg12
  Register #(.width(4)) u_Reg12 (.D(Data_In), .en(Write_Reg12), .Q(Reg12), .clk(CLK));  // open: clr
  // Probe on Reg1
  Register #(.width(4)) u_Reg1 (.D(Data_In), .en(Write_Reg1), .Q(Reg1), .clk(CLK));  // open: clr
  // Probe on Reg5
  Register #(.width(4)) u_Reg5 (.D(Data_In), .en(Write_Reg5), .Q(Reg5), .clk(CLK));  // open: clr
  // Probe on Reg9
  Register #(.width(4)) u_Reg9 (.D(Data_In), .en(Write_Reg9), .Q(Reg9), .clk(CLK));  // open: clr
  // Probe on Reg13
  Register #(.width(4)) u_Reg13 (.D(Data_In), .en(Write_Reg13), .Q(Reg13), .clk(CLK));  // open: clr
  Register #(.width(4)) u_Reg2 (.D(Data_In), .en(Write_Reg2), .Q(Reg2), .clk(CLK));  // open: clr
  Register #(.width(4)) u_Reg6 (.D(Data_In), .en(Write_Reg6), .Q(Reg6), .clk(CLK));  // open: clr
  Register #(.width(4)) u_Reg10 (.D(Data_In), .en(Write_Reg10), .Q(Reg10), .clk(CLK));  // open: clr
  Register #(.width(4)) u_Reg14 (.D(Data_In), .en(Write_Reg14), .Q(Reg14), .clk(CLK));  // open: clr
  // Probe on Reg2
  // Probe on Reg6
  // Probe on Reg10
  // Probe on Reg14
  // Probe on Reg3
  Register #(.width(4)) u_Reg3 (.D(Data_In), .en(Write_Reg3), .Q(Reg3), .clk(CLK));  // open: clr
  // Probe on Reg7
  Register #(.width(4)) u_Reg7 (.D(Data_In), .en(Write_Reg7), .Q(Reg7), .clk(CLK));  // open: clr
  // Probe on Reg11
  Register #(.width(4)) u_Reg11 (.D(Data_In), .en(Write_Reg11), .Q(Reg11), .clk(CLK));  // open: clr
  // Probe on Reg15
  Register #(.width(4)) u_Reg15 (.D(Data_In), .en(Write_Reg15), .Q(Reg15), .clk(CLK));  // open: clr
  Multiplexer #(.select(4), .width(4), .enable("false")) multiplexer_1 (
    .in0(Reg0), .in1(Reg1), .in2(Reg2), .in3(Reg3), .in4(Reg4), .in5(Reg5), .in6(Reg6), .in7(Reg7),
    .in8(Reg8), .in9(Reg9), .in10(Reg10), .in11(Reg11), .in12(Reg12), .in13(Reg13), .in14(Reg14),
    .in15(Reg15), .out(A_DATA), .sel(A));
  Multiplexer #(.select(4), .width(4), .enable("false")) multiplexer_2 (
    .in0(Reg0), .in1(Reg1), .in2(Reg2), .in3(Reg3), .in4(Reg4), .in5(Reg5), .in6(Reg6), .in7(Reg7),
    .in8(Reg8), .in9(Reg9), .in10(Reg10), .in11(Reg11), .in12(Reg12), .in13(Reg13), .in14(Reg14),
    .in15(Reg15), .out(B_DATA), .sel(B));
endmodule

module ALU (
  input  [3:0] OpCode,
  input  [3:0] A,
  input  [3:0] B,
  output [3:0] Answer
);

  wire [3:0] adder_1_out, and_1_out, negator_1_out, not_1_out, or_1_out, subtractor_1_out, xor_1_out;

  assign or_1_out = A | B;  // OR_Gate or_1, 4 bits wide
  Negator #(.width(4)) negator_1 (.in(A), .out(negator_1_out));
  assign and_1_out = A & B;  // AND_Gate and_1, 4 bits wide
  assign xor_1_out = A ^ B;  // XOR_Gate xor_1, 4 bits wide
  Adder #(.width(4)) adder_1 (.a(A), .b(B), .out(adder_1_out));  // open: cin, cout
  assign not_1_out = ~A;  // NOT_Gate not_1, 4 bits wide
  Subtractor #(.width(4)) subtractor_1 (.a(A), .b(B), .out(subtractor_1_out));  // open: bin, bout
  Multiplexer #(.select(4), .width(4), .enable("false")) multiplexer_1 (
    .in0(4'b0000), .in1(4'b0000), .in2(B), .in3(A), .in4(and_1_out), .in5(and_1_out), .in6(or_1_out),
    .in7(or_1_out), .in8(xor_1_out), .in9(xor_1_out), .in10(not_1_out), .in11(negator_1_out),
    .in12(adder_1_out), .in13(adder_1_out), .in14(subtractor_1_out), .in15(subtractor_1_out), .out(Answer),
    .sel(OpCode));

  // Notes on the sheet:
  //   We compute the answer for every possible opcode, then use the opcode as the select bit to select which computation to output
endmodule

module Decoder (
  input  [15:0] Input,
  input  [3:0] Register_B,
  output [3:0] Immediate_B,
  output [3:0] A,
  output [3:0] C,
  output [3:0] Opcode,
  output Halt,
  output RegWrite,
  output [3:0] Chosen_B
);

  Comparator #(.width(4), .mode("unsigned")) comparator_1 (
    .a(Input[15:12]), .b(4'b0001), .gt(RegWrite));  // open: eq, lt
  Comparator #(.width(4)) comparator_2 (.a(Input[15:12]), .b(4'b0000), .eq(Halt));  // open: gt, lt
  Multiplexer #(.select(4), .width(4), .enable("false")) multiplexer_1 (
    .in0(Register_B), .in1(Register_B), .in2(Input[3:0]), .in3(Register_B), .in4(Register_B),
    .in5(Input[3:0]), .in6(Register_B), .in7(Input[3:0]), .in8(Register_B), .in9(Input[3:0]),
    .in10(Register_B), .in11(Register_B), .in12(Register_B), .in13(Input[3:0]), .in14(Register_B),
    .in15(Input[3:0]), .out(Chosen_B), .sel(Input[15:12]));

  assign A = Input[7:4];
  assign C = Input[11:8];
  assign Immediate_B = Input[3:0];
  assign Opcode = Input[15:12];

  // Other names for the same wires on the sheet: Op[3:0] = Input[15:12]

  // Notes on the sheet:
  //   The decoder takes in the opcode and sets regwrite to 1 only if we are currently in any state other than 0000 or 0001
  //   since 0000 and 0001 are the only states where there will be no writing to registers
  //   The decoder will choose  Immediate B for Opcodes [0010,0101,0111,1001,1101,1111] and choose register B otherwise
  //   The decoder takes in the opcode and sets halt to 1 if the state is currently in the halt state which is encoded by OpCode 00000
  //   The chosen B will be used in the ALU Computation
endmodule
